# Fritzing sketch HWMonitor (saved by Fritzing 0.9.3b)

parts:
  Деталь1 = Arduino Nano (Rev3.0)
  RHT1 = Humidity and Temperature Sensor RHT03
  ZS-042_RTC1 = ZS-042 RTC Module
  LCD1 = LCD screen
  LCM1602_IIC1 = LCM1602 IIC [part_number="LCM1602 IIC" chip_label="LCM1602 IIC" package="DIP (Dual Inline) [THT]"]

nets:
  N1: Деталь1.D9, RHT1.Data-signal
  N2: Деталь1.GND, RHT1.GND_2, ZS-042_RTC1.GND#0
  5V: Деталь1.5V, RHT1.Vcc, ZS-042_RTC1.VCC#1
  N3: Деталь1.A5, ZS-042_RTC1.SDA#2
  N4: Деталь1.A4, ZS-042_RTC1.SCL#3
  N5: ZS-042_RTC1.GND#6, LCM1602_IIC1.GND
  N6: ZS-042_RTC1.VCC#7, LCM1602_IIC1.VCC
  N7: ZS-042_RTC1.SDA#8, LCM1602_IIC1.SDA
  N8: ZS-042_RTC1.SCL#9, LCM1602_IIC1.SCL
  VSS: LCD1.VSS, LCM1602_IIC1.VSS
  VDD: LCD1.VDD, LCM1602_IIC1.VDD
  N9: LCD1.V0, LCM1602_IIC1.V0
  N10: LCD1.RS, LCM1602_IIC1.RS
  N11: LCD1.R/W, LCM1602_IIC1.RW
  N12: LCD1.E, LCM1602_IIC1.E
  N13: LCD1.DB0, LCM1602_IIC1.D0
  N14: LCD1.DB1, LCM1602_IIC1.D1
  N15: LCD1.DB2, LCM1602_IIC1.D2
  N16: LCD1.DB3, LCM1602_IIC1.D3
  N17: LCD1.DB4, LCM1602_IIC1.D4
  N18: LCD1.DB5, LCM1602_IIC1.D5
  N19: LCD1.DB6, LCM1602_IIC1.D6
  N20: LCD1.DB7, LCM1602_IIC1.D7
  N21: LCD1.LED+, LCM1602_IIC1.A
  N22: LCD1.LED-, LCM1602_IIC1.K
  N23: LCM1602_IIC1.LED_A, LCM1602_IIC1.LED_B

custom parts:
  LCM1602 IIC: I2C-Module to use a 1602 or 2004 LCD on with the wire.h libory Serial LCD Modul
