# Fritzing sketch Corridor light (saved by Fritzing 0.9.3b)

parts:
  Part1 = Arduino Pro Mini v13
  Part3 = HC-SR501 Body Sensor Module
  Part4 = ws2812b [package="smd 2812b"]
  Part5 = HC-SR501 Body Sensor Module

nets:
  GND: Part1.GND, Part3.GND, Part4.VSS, Part5.GND
  VCC: Part1.VCC, Part3.VCC, Part4.VDD, Part5.VCC
  N1: Part1.D12/MISO, Part3.OUT
  N2: Part1.D11_PWM/MOSI, Part5.OUT
  N3: Part1.D10_PWM/SS, Part4.DIN

custom parts:
  HC-SR501 Body Sensor Module: Pyroelectric Infrared PIR Motion Sensor Detector Module
