# Fritzing sketch layout (saved by Fritzing 0.9.3b)

parts:
  DFRobot_DFPlayer_Mini1 = DFRobot DFPlayer Mini [part_number=DFR0299]
  Part1 = Arduino Pro Mini (5V)
  R1 = Resistor [tolerance=±5% resistance=1k package="2010 [SMD]"]
  R2 = Resistor [tolerance=±5% resistance=1k package="2010 [SMD]"]
  Componente4 = SHT71
  Part6 = HC-SR501 Body Sensor Module
  SP1 = SPEAKER [package=pcb_mount_speaker]
  R7 = Trimmer Potentiometer [maximum_resistance=10kΩ package=THT]
  R8 = Resistor [tolerance=±5% resistance=10k package="2010 [SMD]"]

nets:
  VCC: DFRobot_DFPlayer_Mini1.VCC, Part1.VCC, Componente4.VCC, Part6.VCC, R7.leg2, R8.Pin_0
  N1: DFRobot_DFPlayer_Mini1.RX, R2.Pin_1
  N2: DFRobot_DFPlayer_Mini1.TX, R1.Pin_1
  N3: DFRobot_DFPlayer_Mini1.SPK_1, SP1.-
  GND: DFRobot_DFPlayer_Mini1.GND-1, DFRobot_DFPlayer_Mini1.GND-2, Part1.GND, Componente4.GND, Part6.GND, R7.leg1
  N4: DFRobot_DFPlayer_Mini1.SPK_2, SP1.+
  N5: DFRobot_DFPlayer_Mini1.BUSY, Part1.MISO
  N6: Part1.A0, R7.wiper
  N7: Part1.MOSI, R2.Pin_0
  N8: Part1.D10, R1.Pin_0
  N9: Part1.D9, Part6.OUT
  N10: Part1.D8, Componente4.SCK
  N11: Part1.D7, Componente4.DATA, R8.Pin_1

custom parts:
  HC-SR501 Body Sensor Module: Pyroelectric Infrared PIR Motion Sensor Detector Module
