# Fritzing sketch machine (saved by Fritzing 0.9.3b)

parts:
  Part1 = Arduino Nano (Rev3.0)
  Кнопка_давления = Pushbutton [package="[SMD]"]
  Ручной/Авто = Pushbutton [package="[SMD]"]
  Пуск = Pushbutton [package="[SMD]"]
  К1_вкл = Pushbutton [package="[SMD]"]
  К2_вкл = Pushbutton [package="[SMD]"]
  К3_вкл = Pushbutton [package="[SMD]"]
  К4_вкл = Pushbutton [package="[SMD]"]
  К1 = TLP621 [package=THT]
  К2 = TLP621 [package=THT]
  К3 = TLP621 [package=THT]
  К4 = TLP621 [package=THT]
  К5 = TLP621 [package=THT]
  Уставка_таймер_2 = Trimmer Potentiometer [maximum_resistance=10kΩ package=THT]
  Уставка_таймер_1 = Trimmer Potentiometer [maximum_resistance=10kΩ package=THT]

nets:
  N1: Part1.GND, К1.Pin_2, Уставка_таймер_2.leg1
  N2: Part1.D2, Part1.D3, Part1.D4, Part1.D5, Part1.D6, Part1.D7, Part1.D8, Кнопка_давления.Pin_1, Кнопка_давления.Pin_2, Ручной/Авто.Pin_1, Ручной/Авто.Pin_2, Пуск.Pin_1, Пуск.Pin_2, К1_вкл.Pin_1, К1_вкл.Pin_2, К2_вкл.Pin_1, К2_вкл.Pin_2, К3_вкл.Pin_1, К3_вкл.Pin_2, К4_вкл.Pin_1, К4_вкл.Pin_2, К2.Pin_2, К3.Pin_2, К4.Pin_2, К5.Pin_2
  N3: Part1.D9, К1.Pin_1
  N4: Part1.D10, К2.Pin_1
  N5: Part1.D11/MOSI, К3.Pin_1
  N6: Part1.D12/MISO, К4.Pin_1
  N7: Part1.5V, Уставка_таймер_2.leg2, Уставка_таймер_1.leg2
  N8: Part1.A1, Уставка_таймер_2.wiper
  N9: Part1.A0, Уставка_таймер_1.wiper
  N10: Part1.D13/SCK, К5.Pin_1

notes:
  Таймер 1
  Таймер 2
  К1
  К2
  К3
  К4
  К5
  Кнопка
  давления
  Ручной /
  Авто
  Пуск
  К1
  Вкл
  К2
  Вкл
  К3
  Вкл
  К4
  Вкл
